# Fritzing sketch ledstalk (saved by Fritzing 0.9.0b)
breadboards: 2

parts:
  Composant1 = Arduino Uno (Rev3)  # not connected
  Composant2 = Arduino Leonardo (Rev3b)
  Composant3 = Arduino Ethernet Shield (Rev3)  # not connected
  Composant4 = Arduino ProtoShield
  PIR1 = PIR sensor
  U1 = TMP36 [package=to-92-kit]
  U2 = MAX7219 [package=dil24]
  C1 = Ceramic Capacitor [capacitance=100nF package="100 mil [THT, multilayer]"]
  C2 = Electrolytic Capacitor [capacitance=1µF package="100 mil [THT, electrolytic]"]
  R1 = Resistor [tolerance=±5% resistance=10k package=THT]  # not connected
  R2 = Resistor [tolerance=±5% resistance=27k package=THT]  # not connected
  8x8_LED_Matrix1 = 8x8 LED Matrix 1588ASR

nets:
  N1: Composant2.D2/SDA, Composant4.A4
  N2: Composant2.D3_PWM/SCL, Composant4.A5
  N3: Composant2.D5_PWM, U2.CLK
  N4: Composant2.D6_PWM/A7, U2.LOAD
  N5: Composant2.5V, C1.0, C2.+
  GND: Composant2.GND, Composant4.GND, PIR1.GND, U1.GND
  N6: Composant4.LED2, Composant4.D4
  5V: Composant4.5V, PIR1.VDD, U1.VCC
  N7: Composant4.D2, PIR1.SIG
  N8: Composant4.A0, U1.VOUT
  N9: U2.DIG0, 8x8_LED_Matrix1.Pin_16
  N10: U2.DIG4, 8x8_LED_Matrix1.Pin_10
  N11: U2.DIG6, 8x8_LED_Matrix1.Pin_3
  N12: U2.DIG2, 8x8_LED_Matrix1.Pin_11
  N13: U2.DIG3, 8x8_LED_Matrix1.Pin_6
  N14: U2.DIG7, 8x8_LED_Matrix1.Pin_13
  N15: U2.DIG5, 8x8_LED_Matrix1.Pin_4
  N16: U2.DIG1, 8x8_LED_Matrix1.Pin_15
  N17: U2.SEGA, 8x8_LED_Matrix1.Pin14
  N18: U2.SEGF, 8x8_LED_Matrix1.Pin_2
  N19: U2.SEGB, 8x8_LED_Matrix1.Pin_8
  N20: U2.SEGG, 8x8_LED_Matrix1.Pin_5
  N21: U2.SEGC, 8x8_LED_Matrix1.Pin_12
  N22: U2.SEGE, 8x8_LED_Matrix1.Pin_7
  N23: U2.SEGDP, 8x8_LED_Matrix1.Pin_9
  N24: U2.SEGD, 8x8_LED_Matrix1.Pin_1
  N25: C1.1, C2.-

custom parts:
  8x8 LED Matrix 1588ASR: Red Color Common cathode 8x8 LED Matrix
